// Logisim project cpu.circ as structural Verilog: 1 circuit, main circuit cpu
module cpu (
  input  clk,
  input  [31:0] INSTRUCTION,
  input  [31:0] READ_DATA,
  output [31:0] WRITE_ADDRESS,
  output [31:0] PROGRAM_COUNTER,
  output [31:0] ra,
  output [31:0] sp,
  output [31:0] t0,
  output [31:0] t1,
  output [31:0] t2,
  output [31:0] s0,
  output [31:0] s1,
  output [31:0] a0,
  output [31:0] tohost,
  output [3:0] WRITE_ENABLE,
  output [31:0] WRITE_DATA
);

  wire control_logic_1_p2, control_logic_1_p3, control_logic_1_p5, control_logic_1_p6, control_logic_1_p7,
       control_logic_1_p8, control_logic_1_p9, control_logic_1_p11, control_logic_1_p13, control_logic_1_p14,
       undriven;
  wire [1:0] control_logic_1_p12;
  wire [2:0] control_logic_1_p4;
  wire [3:0] control_logic_1_p10, undriven_2;
  wire [31:0] adder_1_out, adder_2_out, bit_extender_1_out, bit_extender_2_out, imm_gen_1_imm,
       multiplexer_1_out, multiplexer_2_out, multiplexer_3_out, multiplexer_4_out, multiplexer_6_out,
       multiplexer_7_out, regfile_1_read_data_1, register_1_q, register_2_q;

  Multiplexer #(.enable("false"), .width(32)) multiplexer_1 (
    .in0(INSTRUCTION), .in1(32'h13), .out(multiplexer_1_out), .sel(control_logic_1_p2));
  Adder #(.width(32)) adder_1 (.a(PROGRAM_COUNTER), .b(32'h4), .out(adder_1_out));  // open: cin, cout
  Register #(.width(32)) PC (.D(multiplexer_2_out), .clk(clk), .Q(PROGRAM_COUNTER));  // open: en, clr
  Register #(.width(32)) register_1 (.D(multiplexer_1_out), .clk(clk), .Q(register_1_q), .clr(undriven));  // open: en
  Multiplexer #(.enable("false"), .width(32)) multiplexer_2 (
    .in0(adder_1_out), .in1(WRITE_ADDRESS), .out(multiplexer_2_out), .sel(control_logic_1_p2));
  // control_logic control_logic_1: pin names not known; wires that end beside it: register_1_q, control_logic_1_p2, control_logic_1_p3, control_logic_1_p4, control_logic_1_p5, control_logic_1_p6, control_logic_1_p7, control_logic_1_p8, control_logic_1_p9, control_logic_1_p10, control_logic_1_p11, control_logic_1_p12, control_logic_1_p13, control_logic_1_p14
  imm_gen imm_gen_1 (.inst(register_1_q), .ImmSel(control_logic_1_p4), .imm(imm_gen_1_imm));
  regfile regfile_1 (
    .rs1(register_1_q[19:15]), .rs2(register_1_q[24:20]), .rd(register_1_q[11:7]),
    .Write_Data(multiplexer_6_out), .RegWEn(control_logic_1_p3), .clk(clk), .ra(ra), .sp(sp), .t0(t0),
    .t1(t1), .t2(t2), .s0(s0), .s1(s1), .a0(a0), .Read_Data_1(regfile_1_read_data_1), .Read_Data_2(WRITE_DATA));
  Register #(.width(32)) register_2 (.D(PROGRAM_COUNTER), .clk(clk), .Q(register_2_q));  // open: en, clr
  branch_comp branch_comp_1 (
    .rs1(regfile_1_read_data_1), .rs2(WRITE_DATA), .BrUn(control_logic_1_p7), .BrEq(control_logic_1_p5),
    .BrLt(control_logic_1_p6));
  Adder #(.width(32)) adder_2 (.a(32'h4), .b(register_2_q), .out(adder_2_out));  // open: cin, cout
  Multiplexer #(.enable("false"), .width(32)) multiplexer_3 (
    .in0(regfile_1_read_data_1), .in1(register_2_q), .out(multiplexer_3_out), .sel(control_logic_1_p8));
  Multiplexer #(.enable("false"), .width(32)) multiplexer_4 (
    .in0(WRITE_DATA), .in1(imm_gen_1_imm), .out(multiplexer_4_out), .sel(control_logic_1_p9));
  // csr csr_1: pin names not known; wires that end beside it: control_logic_1_p13, WRITE_ADDRESS, control_logic_1_p14, clk, tohost
  alu alu_1 (.Result(WRITE_ADDRESS), .A(multiplexer_3_out), .B(multiplexer_4_out), .ALUSel(control_logic_1_p10));
  Multiplexer #(.enable("false"), .width(4)) multiplexer_5 (
    .in0(4'b0000), .in1(undriven_2), .out(WRITE_ENABLE), .sel(control_logic_1_p11));
  Multiplexer #(.enable("false"), .select(2), .width(32)) multiplexer_6 (
    .in0(multiplexer_7_out), .in1(WRITE_ADDRESS), .in2(adder_2_out), .in3(tohost), .out(multiplexer_6_out),
    .sel(control_logic_1_p12));
  Multiplexer #(.enable("false"), .select(4), .width(32)) multiplexer_7 (
    .in1(bit_extender_1_out), .in3(bit_extender_2_out), .in15(READ_DATA), .out(multiplexer_7_out),
    .sel(undriven_2));  // open: in0, in2, in4, in5, in6, in7, in8, in9, in10, in11, in12, in13, in14
  assign bit_extender_1_out = {{24{READ_DATA[7]}}, READ_DATA[7:0]};  // Bit_Extender bit_extender_1
  assign bit_extender_2_out = {{16{READ_DATA[15]}}, READ_DATA[15:0]};  // Bit_Extender bit_extender_2

  // Notes on the sheet:
  //   Output to IMEM
  //   IMEM (do **NOT** move this)
  //   Inputs from IMEM
  //   It is OK to move the PC, RegFile, ALU, MEM, Branch Comp, Imm Gen, and Control Logic to wherever is most convenient for you when constructing your CPU, and to delete this text
  //   Inputs/Outputs for testing. Do **NOT** move these.
  //   Outputs To DMEM
  //   DMEM (do **NOT** move this)
  //   Inputs From DMEM
endmodule
