// Logisim project imm_gen.circ as structural Verilog: 1 circuit, main circuit imm_gen
module imm_gen (
  input  [31:0] inst,
  input  [2:0] ImmSel,
  output [31:0] imm,
  output [31:0] out_4
);

  wire [12:1] demultiplexer_1_out2_2;
  wire [24:0] demultiplexer_1_out2;
  wire [31:0] demultiplexer_1_out0, demultiplexer_1_out1, imm_I, imm_S, imm_SB;

  Demultiplexer #(.enable("false"), .select(3), .width(32)) demultiplexer_1 (
    .out0(demultiplexer_1_out0), .out1(demultiplexer_1_out1),
    .out2({demultiplexer_1_out2_2[12], demultiplexer_1_out2_2[10:5], demultiplexer_1_out2[24:12], demultiplexer_1_out2_2[4:1], demultiplexer_1_out2_2[11], demultiplexer_1_out2[6:0]}),
    .in(inst), .sel(ImmSel));  // open: out3, out4, out5, out6, out7
  assign imm_I = {{20{demultiplexer_1_out0[31]}}, demultiplexer_1_out0[31:20]};  // Bit_Extender bit_extender_1
  assign imm_S = {{20{demultiplexer_1_out1[31]}}, {demultiplexer_1_out1[31:25], demultiplexer_1_out1[11:7]}};  // Bit_Extender bit_extender_2
  assign imm_SB = {{19{demultiplexer_1_out2_2[12]}}, {demultiplexer_1_out2_2, 1'b0}};  // Bit_Extender bit_extender_3
  or or_1 (imm[0], imm_I[0], imm_S[0], imm_SB[0]);
  or or_2 (imm[1], imm_I[1], imm_S[1], imm_SB[1]);
  or or_3 (imm[2], imm_I[2], imm_S[2], imm_SB[2]);
  or or_4 (imm[3], imm_I[3], imm_S[3], imm_SB[3]);
  or or_5 (imm[4], imm_I[4], imm_S[4], imm_SB[4]);
  or or_6 (imm[5], imm_I[5], imm_S[5], imm_SB[5]);
  or or_7 (imm[6], imm_I[6], imm_S[6], imm_SB[6]);
  or or_8 (imm[7], imm_I[7], imm_S[7], imm_SB[7]);
  or or_9 (imm[8], imm_I[8], imm_S[8], imm_SB[8]);
  or or_10 (imm[9], imm_I[9], imm_S[9], imm_SB[9]);
  or or_11 (imm[10], imm_I[10], imm_S[10], imm_SB[10]);
  or or_12 (imm[11], imm_I[11], imm_S[11], imm_SB[11]);
  or or_13 (imm[12], imm_I[12], imm_S[12], imm_SB[12]);
  or or_14 (imm[13], imm_I[13], imm_S[13], imm_SB[13]);
  or or_15 (imm[14], imm_I[14], imm_S[14], imm_SB[14]);
  or or_16 (imm[15], imm_I[15], imm_S[15], imm_SB[15]);
  or or_17 (imm[16], imm_I[16], imm_S[16], imm_SB[16]);
  or or_18 (imm[17], imm_I[17], imm_S[17], imm_SB[17]);
  or or_19 (imm[18], imm_I[18], imm_S[18], imm_SB[18]);
  or or_20 (imm[19], imm_I[19], imm_S[19], imm_SB[19]);
  or or_21 (imm[20], imm_I[20], imm_S[20], imm_SB[20]);
  or or_22 (imm[21], imm_I[21], imm_S[21], imm_SB[21]);
  or or_23 (imm[22], imm_I[22], imm_S[22], imm_SB[22]);
  or or_24 (imm[23], imm_I[23], imm_S[23], imm_SB[23]);
  or or_25 (imm[24], imm_I[24], imm_S[24], imm_SB[24]);
  or or_26 (imm[25], imm_I[25], imm_S[25], imm_SB[25]);
  or or_27 (imm[26], imm_I[26], imm_S[26], imm_SB[26]);
  or or_28 (imm[27], imm_I[27], imm_S[27], imm_SB[27]);
  or or_29 (imm[28], imm_I[28], imm_S[28], imm_SB[28]);
  or or_30 (imm[29], imm_I[29], imm_S[29], imm_SB[29]);
  or or_31 (imm[30], imm_I[30], imm_S[30], imm_SB[30]);
  or or_32 (imm[31], imm_I[31], imm_S[31], imm_SB[31]);

  assign out_4 = imm;

  // Other names for the same wires on the sheet: imm_0 = imm[0]; imm_7_0[7:0] = imm[7:0]; imm_1 = imm[1];
  //   imm_2 = imm[2]; imm_3 = imm[3]; imm_4 = imm[4]; imm_5 = imm[5]; imm_6 = imm[6]; imm_7 = imm[7]; imm_8 = imm[8];
  //   imm_15_8[7:0] = imm[15:8]; imm_9 = imm[9]; imm_10 = imm[10]; imm_11 = imm[11]; imm_12 = imm[12];
  //   imm_13 = imm[13]; imm_14 = imm[14]; imm_15 = imm[15]; imm_16 = imm[16]; imm_23_16[7:0] = imm[23:16];
  //   imm_17 = imm[17]; imm_18 = imm[18]; imm_19 = imm[19]; imm_20 = imm[20]; imm_21 = imm[21]; imm_22 = imm[22];
  //   imm_23 = imm[23]; imm_24 = imm[24]; imm_31_24[7:0] = imm[31:24]; imm_25 = imm[25]; imm_26 = imm[26];
  //   imm_27 = imm[27]; imm_28 = imm[28]; imm_29 = imm[29]; imm_30 = imm[30]; imm_31 = imm[31]

  // Notes on the sheet:
  //   INPUTS to your circuit
  //   DON'T CHANGE THE LOCATIONS OF THE INPUTS AND OUTPUTS!
  //   OUTPUT from your circuit
endmodule
