// Logisim project regfile.circ as structural Verilog: 1 circuit, main circuit regfile
module regfile (
  input  [4:0] rs1,
  input  [4:0] rs2,
  input  [4:0] rd,
  input  [31:0] Write_Data,
  input  RegWEn,
  input  clk,
  output [31:0] ra,
  output [31:0] sp,
  output [31:0] t0,
  output [31:0] t1,
  output [31:0] t2,
  output [31:0] s0,
  output [31:0] s1,
  output [31:0] a0,
  output [31:0] Read_Data_1,
  output [31:0] Read_Data_2
);

  wire x0write_en, x1write_en, x2write_en, x3write_en, x4write_en, x5write_en, x6write_en, x7write_en,
       x8write_en, x9write_en, x10write_en, x11write_en, x12write_en, x13write_en, x14write_en, x15write_en,
       x16write_en, x17write_en, x18write_en, x19write_en, x20write_en, x21write_en, x22write_en,
       x23write_en, x24write_en, x25write_en, x26write_en, x27write_en, x28write_en, x29write_en,
       x30write_en, x31write_en;
  wire [31:0] x0read_data1;

  Demultiplexer #(.enable("false"), .select(5)) demultiplexer_1 (
    .out0(x0write_en), .out1(x1write_en), .out2(x2write_en), .out3(x3write_en), .out4(x4write_en),
    .out5(x5write_en), .out6(x6write_en), .out7(x7write_en), .out8(x8write_en), .out9(x9write_en),
    .out10(x10write_en), .out11(x11write_en), .out12(x12write_en), .out13(x13write_en), .out14(x14write_en),
    .out15(x15write_en), .out16(x16write_en), .out17(x17write_en), .out18(x18write_en), .out19(x19write_en),
    .out20(x20write_en), .out21(x21write_en), .out22(x22write_en), .out23(x23write_en), .out24(x24write_en),
    .out25(x25write_en), .out26(x26write_en), .out27(x27write_en), .out28(x28write_en), .out29(x29write_en),
    .out30(x30write_en), .out31(x31write_en), .in(RegWEn));  // open: sel
  Register #(.width(32)) x0 (.D(Write_Data), .en(x0write_en), .clk(clk), .Q(x0read_data1));  // open: clr

  // Other names for the same wires on the sheet: read_data1[31:0] = Read_Data_1; read_data2[31:0] = Read_Data_2;
  //   read_reg1[4:0] = rs1; read_reg2[4:0] = rs2; write_en = RegWEn; write_reg[4:0] = rd;
  //   x0read_data2[31:0] = x0read_data1

  // Notes on the sheet:
  //   INPUTS to your circuit
  //   DON'T CHANGE THE LOCATIONS OF THE INPUTS AND OUTPUTS!
  //   These are DEBUG/TEST outputs from your circuit.
  //   OUTPUTS from your circuit
endmodule
